// Logisim project TallerLogica-Combinatorios.circ as structural Verilog: 12 circuits, main circuit verificador
module verificador (
  output [3:0] out_1,
  output [3:0] out_2,
  output [1:0] out_3,
  output halt,
  output N,
  output Z,
  output V,
  output C,
  output [3:0] res
);

  wire clock_1_out;

  Clock clock_1 (.out(clock_1_out));
  Counter #(.max('h3ff), .width(10)) counter_1 (
    .clk(clock_1_out), .carry(halt), .Q({out_3, out_2, out_1}));  // open: clr, load, up, count, D
  ALU alu_1 (.A(out_1), .B(out_2), .OP(out_3), .V(V), .C(C), .N(N), .Z(Z), .S(res));
endmodule

module sumador_completo (
  input  Cin,
  input  A,
  input  B,
  output S,
  output Cout
);

  wire sumador_simple_1_cout, sumador_simple_1_s, sumador_simple_2_cout;

  sumador_simple sumador_simple_1 (.A(A), .B(B), .S(sumador_simple_1_s), .Cout(sumador_simple_1_cout));
  sumador_simple sumador_simple_2 (.A(Cin), .B(sumador_simple_1_s), .S(S), .Cout(sumador_simple_2_cout));
  or or_1 (Cout, sumador_simple_2_cout, sumador_simple_1_cout);
endmodule

module sumador_4 (
  input  Cin,
  input  [3:0] A,
  input  [3:0] B,
  output [3:0] S,
  output Cout
);

  wire sumador_completo_1_cout, sumador_completo_2_cout, sumador_completo_3_cout;

  sumador_completo sumador_completo_1 (.Cin(Cin), .A(A[0]), .B(B[0]), .S(S[0]), .Cout(sumador_completo_1_cout));
  sumador_completo sumador_completo_2 (
    .Cin(sumador_completo_1_cout), .A(A[1]), .B(B[1]), .S(S[1]), .Cout(sumador_completo_2_cout));
  sumador_completo sumador_completo_3 (
    .Cin(sumador_completo_2_cout), .A(A[2]), .B(B[2]), .S(S[2]), .Cout(sumador_completo_3_cout));
  Hex_Digit_Display hex_digit_display_1 (.value(S));  // open: dp
  sumador_completo sumador_completo_4 (.Cin(sumador_completo_3_cout), .A(A[3]), .B(B[3]), .S(S[3]), .Cout(Cout));
endmodule

module comparador_cero (
  input  [3:0] in_1,
  output out_2
);

  nor nor_1 (out_2, in_1[0], in_1[1], in_1[2], in_1[3]);
endmodule

module sumador_simple (
  input  A,
  input  B,
  output S,
  output Cout
);

  xor xor_1 (S, A, B);
  and and_1 (Cout, A, B);
endmodule

module sumador_flags (
  input  Cin,
  input  [3:0] A,
  input  [3:0] B,
  output C,
  output [3:0] S,
  output Z,
  output N,
  output V
);

  sumador_4 sumador_4_1 (.Cin(Cin), .A(A), .B(B), .S({N, S[2:0]}), .Cout(C));
  Overflow overflow_1 (.A(A[3]), .B(B[3]), .C(N), .N(V));
  Hex_Digit_Display hex_digit_display_1 (.value({N, S[2:0]}));  // open: dp
  comparador_cero comparador_cero_1 (.in_1({N, S[2:0]}), .out_2(Z));

  assign S[3] = N;
endmodule

module incrementador_4 (
  input  [3:0] A,
  output [3:0] S
);

  sumador_4 sumador_4_1 (.A(A), .B(4'b0001), .S(S));  // open: Cin, Cout
  Hex_Digit_Display hex_digit_display_1 (.value(S));  // open: dp
endmodule

module inversor_4 (
  input  [3:0] A,
  input  INV,
  output [3:0] S
);

  wire [3:0] incrementador_4_1_s, xor_4_out;

  xor xor_1 (xor_4_out[3], INV, A[3]);
  xor xor_2 (xor_4_out[1], A[1], INV);
  xor xor_3 (xor_4_out[2], INV, A[2]);
  xor xor_4 (xor_4_out[0], A[0], INV);
  incrementador_4 incrementador_4_1 (.A(xor_4_out), .S(incrementador_4_1_s));
  Multiplexer #(.width(4)) multiplexer_1 (.in0(A), .in1(incrementador_4_1_s), .out(S), .sel(INV));
  Hex_Digit_Display hex_digit_display_1 (.value(S));  // open: dp
endmodule

module ALU (
  input  [3:0] A,
  input  [3:0] B,
  input  [1:0] OP,
  output V,
  output C,
  output N,
  output Z,
  output [3:0] S
);

  wire comparador_cero_1_out_2, comparador_cero_2_out_2, multiplexer_4_out, nor_1_out, not_2_out,
       sumador_flags_1_c, sumador_flags_1_v;
  wire [3:0] a_and_b_1_s, a_or_b_1_s, inversor_4_1_s, sumador_flags_1_s;
  wire [3:3] not_1_out;

  comparador_cero comparador_cero_1 (.in_1(B), .out_2(comparador_cero_1_out_2));
  inversor_4 inversor_4_1 (.A(B), .INV(OP[0]), .S(inversor_4_1_s));
  not not_1 (not_1_out[3], B[3]);
  a_or_b a_or_b_1 (.A(A), .B(B), .S(a_or_b_1_s));
  a_and_b a_and_b_1 (.A(A), .B(B), .S(a_and_b_1_s));
  sumador_flags sumador_flags_1 (
    .A(A), .B(inversor_4_1_s), .C(sumador_flags_1_c), .S(sumador_flags_1_s), .V(sumador_flags_1_v));  // open: Cin, Z, N
  nor nor_1 (nor_1_out, sumador_flags_1_c, comparador_cero_1_out_2);
  Multiplexer #(.select(2), .width(4)) multiplexer_1 (
    .in0(sumador_flags_1_s), .in1(sumador_flags_1_s), .in2(a_and_b_1_s), .in3(a_or_b_1_s), .out({N, S[2:0]}),
    .sel(OP));
  comparador_cero comparador_cero_2 (.in_1({not_1_out[3], B[2:0]}), .out_2(comparador_cero_2_out_2));
  Hex_Digit_Display hex_digit_display_1 (.value({N, S[2:0]}));  // open: dp
  not not_2 (not_2_out, sumador_flags_1_v);
  Multiplexer #(.select(2)) multiplexer_2 (
    .in0(sumador_flags_1_v), .in1(multiplexer_4_out), .in2(1'b0), .in3(1'b0), .out(V), .sel(OP));
  Multiplexer #(.select(2)) multiplexer_3 (
    .in0(sumador_flags_1_c), .in1(nor_1_out), .in2(1'b0), .in3(1'b0), .out(C), .sel(OP));
  comparador_cero comparador_cero_3 (.in_1({N, S[2:0]}), .out_2(Z));
  Multiplexer multiplexer_4 (
    .in0(sumador_flags_1_v), .in1(not_2_out), .out(multiplexer_4_out), .sel(comparador_cero_2_out_2));

  assign S[3] = N;
endmodule

module a_and_b (
  input  [3:0] A,
  input  [3:0] B,
  output [3:0] S
);

  and and_1 (S[0], A[0], B[0]);
  and and_2 (S[3], A[3], B[3]);
  and and_3 (S[1], A[1], B[1]);
  and and_4 (S[2], A[2], B[2]);
endmodule

module a_or_b (
  input  [3:0] A,
  input  [3:0] B,
  output [3:0] S
);

  or or_1 (S[0], A[0], B[0]);
  or or_2 (S[3], A[3], B[3]);
  or or_3 (S[1], A[1], B[1]);
  or or_4 (S[2], A[2], B[2]);
endmodule

module Overflow (
  input  A,
  input  B,
  input  C,
  output N
);

  wire and_1_out, and_2_out, and_3_out, and_4_out, not_1_out, not_2_out, not_3_out;

  not not_1 (not_1_out, A);
  not not_2 (not_2_out, B);
  not not_3 (not_3_out, C);
  and and_1 (and_1_out, A, B);
  and and_2 (and_2_out, not_1_out, not_2_out);
  and and_3 (and_3_out, and_1_out, not_3_out);
  and and_4 (and_4_out, and_2_out, C);
  or or_1 (N, and_3_out, and_4_out);
endmodule
